// Logisim project stage1.circ as structural Verilog: 1 circuit, main circuit main
module main (
);

  wire button_1_out, t_ff_1_q;

  Hex_Digit_Display hex_digit_display_1 ();  // open: value, dp
  Hex_Digit_Display hex_digit_display_2 ();  // open: value, dp
  Button button_1 (.out(button_1_out));
  Hex_Digit_Display hex_digit_display_3 ();  // open: value, dp
  Button button_2 ();  // open: out
  Hex_Digit_Display hex_digit_display_4 ();  // open: value, dp
  Button button_3 ();  // open: out
  T_Flip_Flop t_ff_1 (.T(button_1_out), .clk(button_1_out), .Q(t_ff_1_q));  // open: Qn, reset, preset
  Hex_Digit_Display hex_digit_display_5 ();  // open: value, dp
  Hex_Digit_Display hex_digit_display_6 ();  // open: value, dp
  LED led_1 (.in(t_ff_1_q));
  Hex_Digit_Display hex_digit_display_7 ();  // open: value, dp
  Hex_Digit_Display hex_digit_display_8 ();  // open: value, dp

  // Notes on the sheet:
  //   Minutes
  //   Start / Stop
  //   Elapsed Time
  //   :
  //   Stopwatch Interface
  //   Split
  //   Seconds
  //   Reset
  //   Minutes
  //   Split Time
  //   :
  //   Clock Started
  //   Seconds
endmodule
