// Logisim project stage2.circ as structural Verilog: 2 circuits, main circuit main
module main (
);

  wire button_1_out, t_ff_1_q;
  wire [3:0] seconds09_1_r0;

  Button button_1 (.out(button_1_out));
  T_Flip_Flop t_ff_1 (.T(button_1_out), .clk(button_1_out), .Q(t_ff_1_q));  // open: Qn, reset, preset
  Clock clock_1 ();  // open: out
  Button button_2 ();  // open: out
  Button button_3 ();  // open: out
  Hex_Digit_Display hex_digit_display_1 ();  // open: value, dp
  Hex_Digit_Display hex_digit_display_2 ();  // open: value, dp
  Hex_Digit_Display hex_digit_display_3 ();  // open: value, dp
  Hex_Digit_Display hex_digit_display_4 (.value(seconds09_1_r0));  // open: dp
  seconds09 seconds09_1 (
    .CLK(t_ff_1_q), .D(t_ff_1_q), .R3(seconds09_1_r0[3]), .R2(seconds09_1_r0[2]), .R1(seconds09_1_r0[1]),
    .R0(seconds09_1_r0[0]));
  Hex_Digit_Display hex_digit_display_5 ();  // open: value, dp
  Hex_Digit_Display hex_digit_display_6 ();  // open: value, dp
  Hex_Digit_Display hex_digit_display_7 ();  // open: value, dp
  Hex_Digit_Display hex_digit_display_8 ();  // open: value, dp

  // Notes on the sheet:
  //   Start / Stop
  //   Stopwatch Interface
  //   Split
  //   Reset
  //   Minutes
  //   Elapsed Time
  //   :
  //   Seconds
  //   Split Time
  //   Minutes
  //   :
  //   Seconds
endmodule

module seconds09 (
  input  CLK,
  input  D,
  output R3,
  output R2,
  output R1,
  output R0
);

  wire and_1_out, and_2_out, and_3_out, and_4_out, clock_1_out, j_k_ff_1_q, j_k_ff_2_q, j_k_ff_3_q,
       j_k_ff_4_q;

  and and_1 (and_1_out, j_k_ff_1_q, j_k_ff_3_q);
  D_Flip_Flop d_ff_1 (.D(j_k_ff_1_q), .clk(and_4_out), .Q(R3));  // open: Qn, preset, reset
  LED led_1 (.in(j_k_ff_1_q));
  J_K_Flip_Flop j_k_ff_1 (
    .J(and_2_out), .K(and_2_out), .clk(and_4_out), .Q(j_k_ff_1_q), .reset(and_1_out));  // open: Qn, preset
  and and_2 (and_2_out, j_k_ff_4_q, j_k_ff_3_q, j_k_ff_2_q);
  J_K_Flip_Flop j_k_ff_2 (
    .J(and_3_out), .K(and_3_out), .clk(and_4_out), .Q(j_k_ff_2_q), .reset(and_1_out));  // open: Qn, preset
  D_Flip_Flop d_ff_2 (.D(j_k_ff_2_q), .clk(and_4_out), .Q(R2));  // open: Qn, preset, reset
  LED led_2 (.in(j_k_ff_2_q));
  and and_3 (and_3_out, j_k_ff_4_q, j_k_ff_3_q);
  J_K_Flip_Flop j_k_ff_3 (
    .J(j_k_ff_4_q), .K(j_k_ff_4_q), .clk(and_4_out), .Q(j_k_ff_3_q), .reset(and_1_out));  // open: Qn, preset
  D_Flip_Flop d_ff_3 (.D(j_k_ff_3_q), .clk(and_4_out), .Q(R1));  // open: Qn, preset, reset
  LED led_3 (.in(j_k_ff_3_q));
  J_K_Flip_Flop j_k_ff_4 (.J(D), .K(D), .clk(and_4_out), .Q(j_k_ff_4_q), .reset(and_1_out));  // open: Qn, preset
  D_Flip_Flop d_ff_4 (.D(j_k_ff_4_q), .clk(and_4_out), .Q(R0));  // open: Qn, preset, reset
  LED led_4 (.in(j_k_ff_4_q));
  and and_4 (and_4_out, CLK, clock_1_out);
  Clock clock_1 (.out(clock_1_out));

  // Notes on the sheet:
  //   Clear
  //   Buffer
  //   3
  //   2
  //   1
  //   Start
  //   0
endmodule
