// Logisim project stage5.circ as structural Verilog: 7 circuits, main circuit main
module main (
);

  wire button_1_out, button_2_out, button_3_out, minutes09_1_c3, seconds05_1_c2, seconds09_1_c1, t_ff_1_q;
  wire [3:0] minutes09_1_r0, minutes092_1_r0, seconds05_1_r0, seconds09_1_r0, splitminutes_1_o0,
       splitminutes_1_o4, splitseconds_1_o0, splitseconds_1_o4;

  Button button_1 (.out(button_1_out));
  T_Flip_Flop t_ff_1 (.T(button_2_out), .clk(button_2_out), .Q(t_ff_1_q), .reset(button_3_out));  // open: Qn, preset
  Button button_2 (.out(button_2_out));
  Button button_3 (.out(button_3_out));
  minutes092 minutes092_1 (
    .clk(t_ff_1_q), .MReset(button_3_out), .C1(seconds09_1_c1), .C2(seconds05_1_c2), .C3(minutes09_1_c3),
    .R3(minutes092_1_r0[3]), .R2(minutes092_1_r0[2]), .R1(minutes092_1_r0[1]), .R0(minutes092_1_r0[0]));
  Clock clock_1 ();  // open: out
  minutes09 minutes09_1 (
    .clk(t_ff_1_q), .MReset(button_3_out), .C2(seconds05_1_c2), .C1(seconds09_1_c1), .C3(minutes09_1_c3),
    .R3(minutes09_1_r0[3]), .R2(minutes09_1_r0[2]), .R1(minutes09_1_r0[1]), .R0(minutes09_1_r0[0]));
  Hex_Digit_Display hex_digit_display_1 (.value(minutes092_1_r0));  // open: dp
  Hex_Digit_Display hex_digit_display_2 (.value(minutes09_1_r0));  // open: dp
  Hex_Digit_Display hex_digit_display_3 (.value(seconds05_1_r0));  // open: dp
  seconds05 seconds05_1 (
    .clk(t_ff_1_q), .MReset(button_3_out), .Cin(seconds09_1_c1), .C2(seconds05_1_c2), .R3(seconds05_1_r0[3]),
    .R2(seconds05_1_r0[2]), .R1(seconds05_1_r0[1]), .R0(seconds05_1_r0[0]));  // open: in_1
  Hex_Digit_Display hex_digit_display_4 (.value(seconds09_1_r0));  // open: dp
  seconds09 seconds09_1 (
    .MReset(button_3_out), .CLK(t_ff_1_q), .D(t_ff_1_q), .R3(seconds09_1_r0[3]), .R2(seconds09_1_r0[2]),
    .R1(seconds09_1_r0[1]), .R0(seconds09_1_r0[0]), .C1(seconds09_1_c1));
  Hex_Digit_Display hex_digit_display_5 (.value(splitminutes_1_o4));  // open: dp
  Hex_Digit_Display hex_digit_display_6 (.value(splitminutes_1_o0));  // open: dp
  Hex_Digit_Display hex_digit_display_7 (.value(splitseconds_1_o4));  // open: dp
  Hex_Digit_Display hex_digit_display_8 (.value(splitseconds_1_o0));  // open: dp
  splitminutes splitminutes_1 (
    .M7(minutes092_1_r0[3]), .M6(minutes092_1_r0[2]), .M5(minutes092_1_r0[1]), .M4(minutes092_1_r0[0]),
    .M3(minutes09_1_r0[3]), .M2(minutes09_1_r0[2]), .M1(minutes09_1_r0[1]), .M0(minutes09_1_r0[0]),
    .Split(button_1_out), .CLK(t_ff_1_q), .MReset(button_3_out), .O7(splitminutes_1_o4[3]),
    .O6(splitminutes_1_o4[2]), .O5(splitminutes_1_o4[1]), .O4(splitminutes_1_o4[0]),
    .O3(splitminutes_1_o0[3]), .O2(splitminutes_1_o0[2]), .O1(splitminutes_1_o0[1]), .O0(splitminutes_1_o0[0]));
  splitseconds splitseconds_1 (
    .S7(seconds05_1_r0[3]), .S6(seconds05_1_r0[2]), .S5(seconds05_1_r0[1]), .S4(seconds05_1_r0[0]),
    .S3(seconds09_1_r0[3]), .S2(seconds09_1_r0[1]), .S1(seconds09_1_r0[1]), .S0(seconds09_1_r0[0]),
    .Split(button_1_out), .CLK(t_ff_1_q), .MReset(button_3_out), .O7(splitseconds_1_o4[3]),
    .O6(splitseconds_1_o4[2]), .O5(splitseconds_1_o4[1]), .O4(splitseconds_1_o4[0]),
    .O3(splitseconds_1_o0[3]), .O2(splitseconds_1_o0[2]), .O1(splitseconds_1_o0[1]), .O0(splitseconds_1_o0[0]));

  // Notes on the sheet:
  //   Split
  //   Start / Stop
  //   Reset
  //   Minutes
  //   Stopwatch Interface
  //   Elapsed Time
  //   Seconds
  //   :
  //   Minutes
  //   Split Time
  //   :
  //   Seconds
endmodule

module seconds09 (
  input  MReset,
  input  CLK,
  input  D,
  output R3,
  output R2,
  output R1,
  output R0,
  output C1
);

  wire and_1_out, and_2_out, and_3_out, and_4_out, clock_1_out, j_k_ff_1_q, j_k_ff_2_q, j_k_ff_3_q,
       j_k_ff_4_q, or_1_out;

  and and_1 (and_1_out, j_k_ff_1_q, j_k_ff_3_q);
  or or_1 (or_1_out, and_1_out, MReset);
  D_Flip_Flop d_ff_1 (.D(j_k_ff_1_q), .clk(and_4_out), .Q(R3), .reset(MReset));  // open: Qn, preset
  LED led_1 (.in(j_k_ff_1_q));
  J_K_Flip_Flop j_k_ff_1 (
    .J(and_2_out), .K(and_2_out), .clk(and_4_out), .Q(j_k_ff_1_q), .reset(or_1_out));  // open: Qn, preset
  and and_2 (and_2_out, j_k_ff_4_q, j_k_ff_3_q, j_k_ff_2_q);
  J_K_Flip_Flop j_k_ff_2 (
    .J(and_3_out), .K(and_3_out), .clk(and_4_out), .Q(j_k_ff_2_q), .reset(or_1_out));  // open: Qn, preset
  D_Flip_Flop d_ff_2 (.D(j_k_ff_2_q), .clk(and_4_out), .Q(R2), .reset(MReset));  // open: Qn, preset
  LED led_2 (.in(j_k_ff_2_q));
  and and_3 (and_3_out, j_k_ff_4_q, j_k_ff_3_q);
  J_K_Flip_Flop j_k_ff_3 (
    .J(j_k_ff_4_q), .K(j_k_ff_4_q), .clk(and_4_out), .Q(j_k_ff_3_q), .reset(or_1_out));  // open: Qn, preset
  D_Flip_Flop d_ff_3 (.D(j_k_ff_3_q), .clk(and_4_out), .Q(R1), .reset(MReset));  // open: Qn, preset
  LED led_3 (.in(j_k_ff_3_q));
  J_K_Flip_Flop j_k_ff_4 (.J(D), .K(D), .clk(and_4_out), .Q(j_k_ff_4_q), .reset(or_1_out));  // open: Qn, preset
  D_Flip_Flop d_ff_4 (.D(j_k_ff_4_q), .clk(and_4_out), .Q(R0), .reset(MReset));  // open: Qn, preset
  LED led_4 (.in(j_k_ff_4_q));
  and and_4 (and_4_out, CLK, clock_1_out);
  and and_5 (C1, R0, R3);
  Clock clock_1 (.out(clock_1_out));

  // Notes on the sheet:
  //   0 - 9 Decimal
  //   3
  //   2
  //   1
  //   Start
  //   0
endmodule

module seconds05 (
  input  in_1,
  input  clk,
  input  MReset,
  input  Cin,
  output C2,
  output R3,
  output R2,
  output R1,
  output R0
);

  wire and_1_out, and_2_out, and_3_out, clock_1_out, j_k_ff_1_q, j_k_ff_2_q, j_k_ff_3_q, or_1_out;

  Clock clock_1 (.out(clock_1_out));
  and and_1 (and_1_out, clk, clock_1_out);
  or or_1 (or_1_out, MReset, and_2_out);
  and and_2 (and_2_out, j_k_ff_2_q, j_k_ff_1_q);
  D_Flip_Flop d_ff_1 (.D(j_k_ff_1_q), .clk(and_1_out), .Q(R2), .reset(MReset));  // open: Qn, preset
  LED led_1 (.in(j_k_ff_1_q));
  J_K_Flip_Flop j_k_ff_1 (
    .J(and_3_out), .K(and_3_out), .clk(Cin), .Q(j_k_ff_1_q), .reset(or_1_out));  // open: Qn, preset
  and and_3 (and_3_out, j_k_ff_3_q, j_k_ff_2_q);
  J_K_Flip_Flop j_k_ff_2 (
    .J(j_k_ff_3_q), .K(j_k_ff_3_q), .clk(Cin), .Q(j_k_ff_2_q), .reset(or_1_out));  // open: Qn, preset
  D_Flip_Flop d_ff_2 (.D(j_k_ff_2_q), .clk(and_1_out), .Q(R1), .reset(MReset));  // open: Qn, preset
  LED led_2 (.in(j_k_ff_2_q));
  and and_4 (C2, R2, R0);
  J_K_Flip_Flop j_k_ff_3 (.J(1'b1), .K(1'b1), .clk(Cin), .Q(j_k_ff_3_q), .reset(or_1_out));  // open: Qn, preset
  D_Flip_Flop d_ff_3 (.D(j_k_ff_3_q), .clk(and_1_out), .Q(R0), .reset(MReset));  // open: Qn, preset
  LED led_3 (.in(j_k_ff_3_q));

  assign R3 = in_1;

  // Notes on the sheet:
  //   2
  //   1
  //   0
endmodule

module minutes09 (
  input  clk,
  input  MReset,
  input  C2,
  input  C1,
  output C3,
  output R3,
  output R2,
  output R1,
  output R0
);

  wire and_1_out, and_2_out, and_3_out, and_4_out, and_5_out, clock_1_out, j_k_ff_1_q, j_k_ff_2_q,
       j_k_ff_3_q, j_k_ff_4_q, or_1_out;

  Clock clock_1 (.out(clock_1_out));
  and and_1 (and_1_out, clk, clock_1_out);
  and and_2 (and_2_out, j_k_ff_1_q, j_k_ff_3_q);
  or or_1 (or_1_out, MReset, and_2_out);
  and and_3 (and_3_out, C2, C1);
  J_K_Flip_Flop j_k_ff_1 (
    .J(and_4_out), .K(and_4_out), .clk(and_3_out), .Q(j_k_ff_1_q), .reset(or_1_out));  // open: Qn, preset
  D_Flip_Flop d_ff_1 (.D(j_k_ff_1_q), .clk(and_1_out), .Q(R3), .reset(MReset));  // open: Qn, preset
  and and_4 (and_4_out, and_5_out, j_k_ff_2_q);
  LED led_1 (.in(j_k_ff_1_q));
  J_K_Flip_Flop j_k_ff_2 (
    .J(and_5_out), .K(and_5_out), .clk(and_3_out), .Q(j_k_ff_2_q), .reset(or_1_out));  // open: Qn, preset
  D_Flip_Flop d_ff_2 (.D(j_k_ff_2_q), .clk(and_1_out), .Q(R2), .reset(MReset));  // open: Qn, preset
  and and_5 (and_5_out, j_k_ff_4_q, j_k_ff_3_q);
  LED led_2 (.in(j_k_ff_2_q));
  LED led_3 (.in(j_k_ff_3_q));
  J_K_Flip_Flop j_k_ff_3 (
    .J(j_k_ff_4_q), .K(j_k_ff_4_q), .clk(and_3_out), .Q(j_k_ff_3_q), .reset(or_1_out));  // open: Qn, preset
  D_Flip_Flop d_ff_3 (.D(j_k_ff_3_q), .clk(and_1_out), .Q(R1), .reset(MReset));  // open: Qn, preset
  and and_6 (C3, R3, R0);
  D_Flip_Flop d_ff_4 (.D(j_k_ff_4_q), .clk(and_1_out), .Q(R0), .reset(MReset));  // open: Qn, preset
  LED led_4 (.in(j_k_ff_4_q));
  J_K_Flip_Flop j_k_ff_4 (.J(1'b1), .K(1'b1), .clk(and_3_out), .Q(j_k_ff_4_q), .reset(or_1_out));  // open: Qn, preset

  // Notes on the sheet:
  //   3
  //   2
  //   1
  //   0
endmodule

module minutes092 (
  input  clk,
  input  MReset,
  input  C1,
  input  C2,
  input  C3,
  output R3,
  output R2,
  output R1,
  output R0
);

  wire and_1_out, and_2_out, and_3_out, and_4_out, and_5_out, and_6_out, clock_1_out, j_k_ff_1_q, j_k_ff_2_q,
       j_k_ff_3_q, j_k_ff_4_q, or_1_out;

  Clock clock_1 (.out(clock_1_out));
  and and_1 (and_1_out, C1, C2, C3);
  and and_2 (and_2_out, clk, clock_1_out);
  and and_3 (and_3_out, j_k_ff_1_q, j_k_ff_3_q);
  or or_1 (or_1_out, MReset, and_3_out);
  J_K_Flip_Flop j_k_ff_1 (
    .J(and_4_out), .K(and_4_out), .clk(and_1_out), .Q(j_k_ff_1_q), .reset(or_1_out));  // open: Qn, preset
  D_Flip_Flop d_ff_1 (.D(j_k_ff_1_q), .clk(and_2_out), .Q(R3), .reset(MReset));  // open: Qn, preset
  and and_4 (and_4_out, and_5_out, j_k_ff_2_q);
  LED led_1 (.in(j_k_ff_1_q));
  J_K_Flip_Flop j_k_ff_2 (
    .J(and_5_out), .K(and_5_out), .clk(and_1_out), .Q(j_k_ff_2_q), .reset(or_1_out));  // open: Qn, preset
  D_Flip_Flop d_ff_2 (.D(j_k_ff_2_q), .clk(and_2_out), .Q(R2), .reset(MReset));  // open: Qn, preset
  and and_5 (and_5_out, j_k_ff_4_q, j_k_ff_3_q);
  LED led_2 (.in(j_k_ff_2_q));
  J_K_Flip_Flop j_k_ff_3 (
    .J(j_k_ff_4_q), .K(j_k_ff_4_q), .clk(and_1_out), .Q(j_k_ff_3_q), .reset(or_1_out));  // open: Qn, preset
  D_Flip_Flop d_ff_3 (.D(j_k_ff_3_q), .clk(and_2_out), .Q(R1), .reset(MReset));  // open: Qn, preset
  LED led_3 (.in(j_k_ff_3_q));
  and and_6 (and_6_out, R3, R0);
  LED led_4 (.in(j_k_ff_4_q));
  J_K_Flip_Flop j_k_ff_4 (.J(1'b1), .K(1'b1), .clk(and_1_out), .Q(j_k_ff_4_q), .reset(or_1_out));  // open: Qn, preset
  D_Flip_Flop d_ff_4 (.D(j_k_ff_4_q), .clk(and_2_out), .Q(R0), .reset(MReset));  // open: Qn, preset

  // Notes on the sheet:
  //   3
  //   2
  //   1
  //   0
endmodule

module splitminutes (
  input  M7,
  input  M6,
  input  M5,
  input  M4,
  input  M3,
  input  M2,
  input  M1,
  input  M0,
  input  Split,
  input  CLK,
  input  MReset,
  output O7,
  output O6,
  output O5,
  output O4,
  output O3,
  output O2,
  output O1,
  output O0
);

  wire and_1_out;

  and and_1 (and_1_out, Split, CLK);
  D_Flip_Flop d_ff_1 (.D(M7), .clk(and_1_out), .Q(O7), .reset(MReset));  // open: Qn, preset
  D_Flip_Flop d_ff_2 (.D(M6), .clk(and_1_out), .Q(O6), .reset(MReset));  // open: Qn, preset
  LED led_1 (.in(O7));
  LED led_2 (.in(O6));
  D_Flip_Flop d_ff_3 (.D(M5), .clk(and_1_out), .Q(O5), .reset(MReset));  // open: Qn, preset
  D_Flip_Flop d_ff_4 (.D(M4), .clk(and_1_out), .Q(O4), .reset(MReset));  // open: Qn, preset
  LED led_3 (.in(O5));
  LED led_4 (.in(O4));
  D_Flip_Flop d_ff_5 (.D(M3), .clk(and_1_out), .Q(O3), .reset(MReset));  // open: Qn, preset
  LED led_5 (.in(O3));
  D_Flip_Flop d_ff_6 (.D(M2), .clk(and_1_out), .Q(O2), .reset(MReset));  // open: Qn, preset
  D_Flip_Flop d_ff_7 (.D(M1), .clk(and_1_out), .Q(O1), .reset(MReset));  // open: Qn, preset
  LED led_6 (.in(O2));
  D_Flip_Flop d_ff_8 (.D(M0), .clk(and_1_out), .Q(O0), .reset(MReset));  // open: Qn, preset
  LED led_7 (.in(O1));
  LED led_8 (.in(O0));

  // Notes on the sheet:
  //   Ts
  //   3
  //   2
  //   Minutes
  //   1
  //   0
  //   3
  //   1s
  //   2
  //   1
  //   0
endmodule

module splitseconds (
  input  S7,
  input  S6,
  input  S5,
  input  S4,
  input  S3,
  input  S2,
  input  S1,
  input  S0,
  input  Split,
  input  CLK,
  input  MReset,
  output O7,
  output O6,
  output O5,
  output O4,
  output O3,
  output O2,
  output O1,
  output O0
);

  wire and_1_out;

  and and_1 (and_1_out, Split, CLK);
  D_Flip_Flop d_ff_1 (.D(S7), .clk(and_1_out), .Q(O7), .reset(MReset));  // open: Qn, preset
  D_Flip_Flop d_ff_2 (.D(S6), .clk(and_1_out), .Q(O6), .reset(MReset));  // open: Qn, preset
  LED led_1 (.in(O7));
  LED led_2 (.in(O6));
  D_Flip_Flop d_ff_3 (.D(S5), .clk(and_1_out), .Q(O5), .reset(MReset));  // open: Qn, preset
  LED led_3 (.in(O5));
  D_Flip_Flop d_ff_4 (.D(S4), .clk(and_1_out), .Q(O4), .reset(MReset));  // open: Qn, preset
  LED led_4 (.in(O4));
  D_Flip_Flop d_ff_5 (.D(S3), .clk(and_1_out), .Q(O3), .reset(MReset));  // open: Qn, preset
  LED led_5 (.in(O3));
  D_Flip_Flop d_ff_6 (.D(S2), .clk(and_1_out), .Q(O2), .reset(MReset));  // open: Qn, preset
  LED led_6 (.in(O2));
  D_Flip_Flop d_ff_7 (.D(S1), .clk(and_1_out), .Q(O1), .reset(MReset));  // open: Qn, preset
  D_Flip_Flop d_ff_8 (.D(S0), .clk(and_1_out), .Q(O0), .reset(MReset));  // open: Qn, preset
  LED led_7 (.in(O1));
  LED led_8 (.in(O0));

  // Notes on the sheet:
  //   Ts
  //   3
  //   2
  //   Seconds
  //   1
  //   0
  //   3
  //   1s
  //   2
  //   1
  //   0
endmodule
