// Logisim project stage6.circ as structural Verilog: 6 circuits, main circuit main
module main (
);

  wire button_1_out, button_2_out, button_3_out, minutes09_1_c3, seconds05_1_c2, seconds09_1_c1, t_ff_1_q;
  wire [3:0] minutes09_1_r0, minutes092_1_r0, seconds05_1_r0, seconds09_1_r0, splitstack_1_o0,
       splitstack_1_p0, splitstack_1_q0, splitstack_1_r0, splitstack_1_s0, splitstack_2_o0, splitstack_2_p0,
       splitstack_2_q0, splitstack_2_r0, splitstack_2_s0, splitstack_3_o0, splitstack_3_p0, splitstack_3_q0,
       splitstack_3_r0, splitstack_3_s0, splitstack_4_o0, splitstack_4_p0, splitstack_4_q0, splitstack_4_r0,
       splitstack_4_s0;

  T_Flip_Flop t_ff_1 (.T(button_1_out), .clk(button_1_out), .Q(t_ff_1_q), .reset(button_2_out));  // open: Qn, preset
  Button button_1 (.out(button_1_out));
  Button button_2 (.out(button_2_out));
  Button button_3 (.out(button_3_out));
  minutes092 minutes092_1 (
    .Enable(t_ff_1_q), .MReset(button_2_out), .C1(seconds09_1_c1), .C2(seconds05_1_c2), .C3(minutes09_1_c3),
    .R3(minutes092_1_r0[3]), .R2(minutes092_1_r0[2]), .R1(minutes092_1_r0[1]), .R0(minutes092_1_r0[0]));
  Clock clock_1 ();  // open: out
  minutes09 minutes09_1 (
    .Enable(t_ff_1_q), .MReset(button_2_out), .C2(seconds05_1_c2), .C1(seconds09_1_c1), .C3(minutes09_1_c3),
    .R3(minutes09_1_r0[3]), .R2(minutes09_1_r0[2]), .R1(minutes09_1_r0[1]), .R0(minutes09_1_r0[0]));
  Hex_Digit_Display hex_digit_display_1 (.value(minutes092_1_r0));  // open: dp
  Hex_Digit_Display hex_digit_display_2 (.value(minutes09_1_r0));  // open: dp
  Hex_Digit_Display hex_digit_display_3 (.value(seconds05_1_r0));  // open: dp
  seconds05 seconds05_1 (
    .Enable(t_ff_1_q), .MReset(button_2_out), .Cin(seconds09_1_c1), .C2(seconds05_1_c2),
    .R3(seconds05_1_r0[3]), .R2(seconds05_1_r0[2]), .R1(seconds05_1_r0[1]), .R0(seconds05_1_r0[0]));  // open: in_1
  Hex_Digit_Display hex_digit_display_4 (.value(seconds09_1_r0));  // open: dp
  seconds09 seconds09_1 (
    .MReset(button_2_out), .Enable(t_ff_1_q), .D(t_ff_1_q), .R3(seconds09_1_r0[3]), .R2(seconds09_1_r0[2]),
    .R1(seconds09_1_r0[1]), .R0(seconds09_1_r0[0]), .C1(seconds09_1_c1));
  Hex_Digit_Display hex_digit_display_5 (.value(splitstack_4_o0));  // open: dp
  Hex_Digit_Display hex_digit_display_6 (.value(splitstack_3_o0));  // open: dp
  Hex_Digit_Display hex_digit_display_7 (.value(splitstack_1_o0));  // open: dp
  Hex_Digit_Display hex_digit_display_8 (.value(splitstack_2_o0));  // open: dp
  splitstack splitstack_1 (
    .In0(seconds09_1_r0[0]), .Split(button_3_out), .Enable(t_ff_1_q), .In1(seconds09_1_r0[1]),
    .In2(seconds09_1_r0[2]), .In3(seconds09_1_r0[3]), .MReset(button_2_out), .O0(splitstack_1_o0[0]),
    .P0(splitstack_1_p0[0]), .Q0(splitstack_1_q0[0]), .R0(splitstack_1_r0[0]), .S0(splitstack_1_s0[0]),
    .O1(splitstack_1_o0[1]), .P1(splitstack_1_p0[1]), .Q1(splitstack_1_q0[1]), .R1(splitstack_1_r0[1]),
    .S1(splitstack_1_s0[1]), .O2(splitstack_1_o0[2]), .P2(splitstack_1_p0[2]), .Q2(splitstack_1_q0[2]),
    .R2(splitstack_1_r0[2]), .S2(splitstack_1_s0[2]), .O3(splitstack_1_o0[3]), .P3(splitstack_1_p0[3]),
    .Q3(splitstack_1_q0[3]), .R3(splitstack_1_r0[3]), .S3(splitstack_1_s0[3]));
  splitstack splitstack_2 (
    .In0(seconds05_1_r0[0]), .Split(button_3_out), .Enable(t_ff_1_q), .In1(seconds05_1_r0[1]),
    .In2(seconds05_1_r0[2]), .In3(seconds05_1_r0[3]), .MReset(button_2_out), .O0(splitstack_2_o0[0]),
    .P0(splitstack_2_p0[0]), .Q0(splitstack_2_q0[0]), .R0(splitstack_2_r0[0]), .S0(splitstack_2_s0[0]),
    .O1(splitstack_2_o0[1]), .P1(splitstack_2_p0[1]), .Q1(splitstack_2_q0[1]), .R1(splitstack_2_r0[1]),
    .S1(splitstack_2_s0[1]), .O2(splitstack_2_o0[2]), .P2(splitstack_2_p0[2]), .Q2(splitstack_2_q0[2]),
    .R2(splitstack_2_r0[2]), .S2(splitstack_2_s0[2]), .O3(splitstack_2_o0[3]), .P3(splitstack_2_p0[3]),
    .Q3(splitstack_2_q0[3]), .R3(splitstack_2_r0[3]), .S3(splitstack_2_s0[3]));
  splitstack splitstack_3 (
    .In0(minutes09_1_r0[0]), .Split(button_3_out), .Enable(t_ff_1_q), .In1(minutes09_1_r0[1]),
    .In2(minutes09_1_r0[2]), .In3(minutes09_1_r0[3]), .MReset(button_2_out), .O0(splitstack_3_o0[0]),
    .P0(splitstack_3_p0[0]), .Q0(splitstack_3_q0[0]), .R0(splitstack_3_r0[0]), .S0(splitstack_3_s0[0]),
    .O1(splitstack_3_o0[1]), .P1(splitstack_3_p0[1]), .Q1(splitstack_3_q0[1]), .R1(splitstack_3_r0[1]),
    .S1(splitstack_3_s0[1]), .O2(splitstack_3_o0[2]), .P2(splitstack_3_p0[2]), .Q2(splitstack_3_q0[2]),
    .R2(splitstack_3_r0[2]), .S2(splitstack_3_s0[2]), .O3(splitstack_3_o0[3]), .P3(splitstack_3_p0[3]),
    .Q3(splitstack_3_q0[3]), .R3(splitstack_3_r0[3]), .S3(splitstack_3_s0[3]));
  splitstack splitstack_4 (
    .In0(minutes092_1_r0[0]), .Split(button_3_out), .Enable(t_ff_1_q), .In1(minutes092_1_r0[1]),
    .In2(minutes092_1_r0[2]), .In3(minutes092_1_r0[3]), .MReset(button_2_out), .O0(splitstack_4_o0[0]),
    .P0(splitstack_4_p0[0]), .Q0(splitstack_4_q0[0]), .R0(splitstack_4_r0[0]), .S0(splitstack_4_s0[0]),
    .O1(splitstack_4_o0[1]), .P1(splitstack_4_p0[1]), .Q1(splitstack_4_q0[1]), .R1(splitstack_4_r0[1]),
    .S1(splitstack_4_s0[1]), .O2(splitstack_4_o0[2]), .P2(splitstack_4_p0[2]), .Q2(splitstack_4_q0[2]),
    .R2(splitstack_4_r0[2]), .S2(splitstack_4_s0[2]), .O3(splitstack_4_o0[3]), .P3(splitstack_4_p0[3]),
    .Q3(splitstack_4_q0[3]), .R3(splitstack_4_r0[3]), .S3(splitstack_4_s0[3]));
  Hex_Digit_Display hex_digit_display_9 (.value(splitstack_4_o0));  // open: dp
  Hex_Digit_Display hex_digit_display_10 (.value(splitstack_3_o0));  // open: dp
  Hex_Digit_Display hex_digit_display_11 (.value(splitstack_4_p0));  // open: dp
  Hex_Digit_Display hex_digit_display_12 (.value(splitstack_2_o0));  // open: dp
  Hex_Digit_Display hex_digit_display_13 (.value(splitstack_3_p0));  // open: dp
  Hex_Digit_Display hex_digit_display_14 (.value(splitstack_1_o0));  // open: dp
  Hex_Digit_Display hex_digit_display_15 (.value(splitstack_2_p0));  // open: dp
  Hex_Digit_Display hex_digit_display_16 (.value(splitstack_1_p0));  // open: dp
  Hex_Digit_Display hex_digit_display_17 (.value(splitstack_4_q0));  // open: dp
  Hex_Digit_Display hex_digit_display_18 (.value(splitstack_3_q0));  // open: dp
  Hex_Digit_Display hex_digit_display_19 (.value(splitstack_2_q0));  // open: dp
  Hex_Digit_Display hex_digit_display_20 (.value(splitstack_1_q0));  // open: dp
  Hex_Digit_Display hex_digit_display_21 (.value(splitstack_4_r0));  // open: dp
  Hex_Digit_Display hex_digit_display_22 (.value(splitstack_3_r0));  // open: dp
  Hex_Digit_Display hex_digit_display_23 (.value(splitstack_2_r0));  // open: dp
  Hex_Digit_Display hex_digit_display_24 (.value(splitstack_1_r0));  // open: dp
  Hex_Digit_Display hex_digit_display_25 (.value(splitstack_4_s0));  // open: dp
  Hex_Digit_Display hex_digit_display_26 (.value(splitstack_3_s0));  // open: dp
  Hex_Digit_Display hex_digit_display_27 (.value(splitstack_2_s0));  // open: dp
  Hex_Digit_Display hex_digit_display_28 (.value(splitstack_1_s0));  // open: dp

  // Notes on the sheet:
  //   Start / Stop
  //   Reset
  //   Split
  //   Minutes 10's
  //   Minutes
  //   Minutes 1's
  //   Elapsed Time
  //   Seconds
  //   :
  //   Stopwatch Interface
  //   Seconds 10's
  //   Seconds 1's
  //   Split Time
  //   Minutes
  //   :
  //   Seconds
  //   Seconds 1's
  //   Seconds 10's
  //   Minutes 1's
  //   Minutes 10's
  //   Minutes
  //   Minutes
  //   Split Time 1
  //   :
  //   Split Time 2
  //   Seconds
  //   Seconds
  //   Minutes
  //   Split Time 3
  //   Seconds
  //   Minutes
  //   Split Time 4
  //   Seconds
  //   Minutes
  //   Split Time 5
  //   Seconds
endmodule

module seconds09 (
  input  MReset,
  input  Enable,
  input  D,
  output R3,
  output R2,
  output R1,
  output R0,
  output C1
);

  wire and_1_out, and_2_out, and_3_out, and_4_out, clock_1_out, j_k_ff_1_q, j_k_ff_2_q, j_k_ff_3_q,
       j_k_ff_4_q, or_1_out;

  and and_1 (and_1_out, j_k_ff_1_q, j_k_ff_3_q);
  or or_1 (or_1_out, and_1_out, MReset);
  D_Flip_Flop d_ff_1 (.D(j_k_ff_1_q), .clk(and_4_out), .Q(R3), .reset(MReset));  // open: Qn, preset
  LED led_1 (.in(j_k_ff_1_q));
  J_K_Flip_Flop j_k_ff_1 (
    .J(and_2_out), .K(and_2_out), .clk(and_4_out), .Q(j_k_ff_1_q), .reset(or_1_out));  // open: Qn, preset
  and and_2 (and_2_out, j_k_ff_4_q, j_k_ff_3_q, j_k_ff_2_q);
  J_K_Flip_Flop j_k_ff_2 (
    .J(and_3_out), .K(and_3_out), .clk(and_4_out), .Q(j_k_ff_2_q), .reset(or_1_out));  // open: Qn, preset
  D_Flip_Flop d_ff_2 (.D(j_k_ff_2_q), .clk(and_4_out), .Q(R2), .reset(MReset));  // open: Qn, preset
  LED led_2 (.in(j_k_ff_2_q));
  and and_3 (and_3_out, j_k_ff_4_q, j_k_ff_3_q);
  J_K_Flip_Flop j_k_ff_3 (
    .J(j_k_ff_4_q), .K(j_k_ff_4_q), .clk(and_4_out), .Q(j_k_ff_3_q), .reset(or_1_out));  // open: Qn, preset
  D_Flip_Flop d_ff_3 (.D(j_k_ff_3_q), .clk(and_4_out), .Q(R1), .reset(MReset));  // open: Qn, preset
  LED led_3 (.in(j_k_ff_3_q));
  J_K_Flip_Flop j_k_ff_4 (.J(D), .K(D), .clk(and_4_out), .Q(j_k_ff_4_q), .reset(or_1_out));  // open: Qn, preset
  D_Flip_Flop d_ff_4 (.D(j_k_ff_4_q), .clk(and_4_out), .Q(R0), .reset(MReset));  // open: Qn, preset
  LED led_4 (.in(j_k_ff_4_q));
  and and_4 (and_4_out, Enable, clock_1_out);
  and and_5 (C1, R0, R3);
  Clock clock_1 (.out(clock_1_out));

  // Notes on the sheet:
  //   0 - 9 Decimal
  //   3
  //   2
  //   1
  //   Start
  //   0
endmodule

module seconds05 (
  input  in_1,
  input  Enable,
  input  MReset,
  input  Cin,
  output C2,
  output R3,
  output R2,
  output R1,
  output R0
);

  wire and_1_out, and_2_out, and_3_out, clock_1_out, j_k_ff_1_q, j_k_ff_2_q, j_k_ff_3_q, or_1_out;

  Clock clock_1 (.out(clock_1_out));
  and and_1 (and_1_out, Enable, clock_1_out);
  or or_1 (or_1_out, MReset, and_2_out);
  and and_2 (and_2_out, j_k_ff_2_q, j_k_ff_1_q);
  D_Flip_Flop d_ff_1 (.D(j_k_ff_1_q), .clk(and_1_out), .Q(R2), .reset(MReset));  // open: Qn, preset
  LED led_1 (.in(j_k_ff_1_q));
  J_K_Flip_Flop j_k_ff_1 (
    .J(and_3_out), .K(and_3_out), .clk(Cin), .Q(j_k_ff_1_q), .reset(or_1_out));  // open: Qn, preset
  and and_3 (and_3_out, j_k_ff_3_q, j_k_ff_2_q);
  J_K_Flip_Flop j_k_ff_2 (
    .J(j_k_ff_3_q), .K(j_k_ff_3_q), .clk(Cin), .Q(j_k_ff_2_q), .reset(or_1_out));  // open: Qn, preset
  D_Flip_Flop d_ff_2 (.D(j_k_ff_2_q), .clk(and_1_out), .Q(R1), .reset(MReset));  // open: Qn, preset
  LED led_2 (.in(j_k_ff_2_q));
  and and_4 (C2, R2, R0);
  J_K_Flip_Flop j_k_ff_3 (.J(1'b1), .K(1'b1), .clk(Cin), .Q(j_k_ff_3_q), .reset(or_1_out));  // open: Qn, preset
  D_Flip_Flop d_ff_3 (.D(j_k_ff_3_q), .clk(and_1_out), .Q(R0), .reset(MReset));  // open: Qn, preset
  LED led_3 (.in(j_k_ff_3_q));

  assign R3 = in_1;

  // Notes on the sheet:
  //   2
  //   1
  //   0
endmodule

module minutes09 (
  input  Enable,
  input  MReset,
  input  C2,
  input  C1,
  output C3,
  output R3,
  output R2,
  output R1,
  output R0
);

  wire and_1_out, and_2_out, and_3_out, and_4_out, and_5_out, clock_1_out, j_k_ff_1_q, j_k_ff_2_q,
       j_k_ff_3_q, j_k_ff_4_q, or_1_out;

  Clock clock_1 (.out(clock_1_out));
  and and_1 (and_1_out, Enable, clock_1_out);
  and and_2 (and_2_out, j_k_ff_1_q, j_k_ff_3_q);
  or or_1 (or_1_out, MReset, and_2_out);
  and and_3 (and_3_out, C2, C1);
  J_K_Flip_Flop j_k_ff_1 (
    .J(and_4_out), .K(and_4_out), .clk(and_3_out), .Q(j_k_ff_1_q), .reset(or_1_out));  // open: Qn, preset
  D_Flip_Flop d_ff_1 (.D(j_k_ff_1_q), .clk(and_1_out), .Q(R3), .reset(MReset));  // open: Qn, preset
  and and_4 (and_4_out, and_5_out, j_k_ff_2_q);
  LED led_1 (.in(j_k_ff_1_q));
  J_K_Flip_Flop j_k_ff_2 (
    .J(and_5_out), .K(and_5_out), .clk(and_3_out), .Q(j_k_ff_2_q), .reset(or_1_out));  // open: Qn, preset
  D_Flip_Flop d_ff_2 (.D(j_k_ff_2_q), .clk(and_1_out), .Q(R2), .reset(MReset));  // open: Qn, preset
  and and_5 (and_5_out, j_k_ff_4_q, j_k_ff_3_q);
  LED led_2 (.in(j_k_ff_2_q));
  LED led_3 (.in(j_k_ff_3_q));
  J_K_Flip_Flop j_k_ff_3 (
    .J(j_k_ff_4_q), .K(j_k_ff_4_q), .clk(and_3_out), .Q(j_k_ff_3_q), .reset(or_1_out));  // open: Qn, preset
  D_Flip_Flop d_ff_3 (.D(j_k_ff_3_q), .clk(and_1_out), .Q(R1), .reset(MReset));  // open: Qn, preset
  and and_6 (C3, R3, R0);
  D_Flip_Flop d_ff_4 (.D(j_k_ff_4_q), .clk(and_1_out), .Q(R0), .reset(MReset));  // open: Qn, preset
  LED led_4 (.in(j_k_ff_4_q));
  J_K_Flip_Flop j_k_ff_4 (.J(1'b1), .K(1'b1), .clk(and_3_out), .Q(j_k_ff_4_q), .reset(or_1_out));  // open: Qn, preset

  // Notes on the sheet:
  //   3
  //   2
  //   1
  //   0
endmodule

module minutes092 (
  input  Enable,
  input  MReset,
  input  C1,
  input  C2,
  input  C3,
  output R3,
  output R2,
  output R1,
  output R0
);

  wire and_1_out, and_2_out, and_3_out, and_4_out, and_5_out, clock_1_out, j_k_ff_1_q, j_k_ff_2_q,
       j_k_ff_3_q, j_k_ff_4_q, or_1_out;

  Clock clock_1 (.out(clock_1_out));
  and and_1 (and_1_out, C1, C2, C3);
  and and_2 (and_2_out, Enable, clock_1_out);
  and and_3 (and_3_out, j_k_ff_1_q, j_k_ff_3_q);
  or or_1 (or_1_out, MReset, and_3_out);
  J_K_Flip_Flop j_k_ff_1 (
    .J(and_4_out), .K(and_4_out), .clk(and_1_out), .Q(j_k_ff_1_q), .reset(or_1_out));  // open: Qn, preset
  D_Flip_Flop d_ff_1 (.D(j_k_ff_1_q), .clk(and_2_out), .Q(R3), .reset(MReset));  // open: Qn, preset
  and and_4 (and_4_out, and_5_out, j_k_ff_2_q);
  LED led_1 (.in(j_k_ff_1_q));
  J_K_Flip_Flop j_k_ff_2 (
    .J(and_5_out), .K(and_5_out), .clk(and_1_out), .Q(j_k_ff_2_q), .reset(or_1_out));  // open: Qn, preset
  D_Flip_Flop d_ff_2 (.D(j_k_ff_2_q), .clk(and_2_out), .Q(R2), .reset(MReset));  // open: Qn, preset
  and and_5 (and_5_out, j_k_ff_4_q, j_k_ff_3_q);
  LED led_2 (.in(j_k_ff_2_q));
  J_K_Flip_Flop j_k_ff_3 (
    .J(j_k_ff_4_q), .K(j_k_ff_4_q), .clk(and_1_out), .Q(j_k_ff_3_q), .reset(or_1_out));  // open: Qn, preset
  D_Flip_Flop d_ff_3 (.D(j_k_ff_3_q), .clk(and_2_out), .Q(R1), .reset(MReset));  // open: Qn, preset
  LED led_3 (.in(j_k_ff_3_q));
  LED led_4 (.in(j_k_ff_4_q));
  J_K_Flip_Flop j_k_ff_4 (.J(1'b1), .K(1'b1), .clk(and_1_out), .Q(j_k_ff_4_q), .reset(or_1_out));  // open: Qn, preset
  D_Flip_Flop d_ff_4 (.D(j_k_ff_4_q), .clk(and_2_out), .Q(R0), .reset(MReset));  // open: Qn, preset

  // Notes on the sheet:
  //   3
  //   2
  //   1
  //   0
endmodule

module splitstack (
  input  In0,
  input  Split,
  input  Enable,
  input  In1,
  input  In2,
  input  In3,
  input  MReset,
  output O0,
  output P0,
  output Q0,
  output R0,
  output S0,
  output O1,
  output P1,
  output Q1,
  output R1,
  output S1,
  output O2,
  output P2,
  output Q2,
  output R2,
  output S2,
  output O3,
  output P3,
  output Q3,
  output R3,
  output S3
);

  wire and_1_out, and_2_out, and_3_out, and_4_out, and_5_out, and_6_out, and_7_out, and_8_out, and_9_out,
       and_10_out, not_1_out, not_2_out, not_3_out, not_4_out, not_5_out, not_6_out, xor_1_out, xor_2_out,
       xor_3_out, xor_4_out, xor_5_out, xor_6_out, xor_7_out, xor_8_out;

  not not_1 (not_1_out, not_2_out);
  not not_2 (not_2_out, Enable);
  not not_3 (not_3_out, not_2_out);
  and and_1 (and_1_out, S0, not_2_out);
  and and_2 (and_2_out, In0, not_1_out);
  not not_4 (not_4_out, not_2_out);
  not not_5 (not_5_out, not_2_out);
  not not_6 (not_6_out, not_2_out);
  and and_3 (and_3_out, 1'b1, Split, not_3_out);
  and and_4 (and_4_out, Split, not_2_out);
  and and_5 (and_5_out, S1, not_2_out);
  and and_6 (and_6_out, In1, not_4_out);
  and and_7 (and_7_out, S2, not_2_out);
  and and_8 (and_8_out, In2, not_5_out);
  and and_9 (and_9_out, S3, not_2_out);
  and and_10 (and_10_out, In3, not_6_out);
  xor xor_1 (xor_1_out, and_1_out, and_2_out);
  xor xor_2 (xor_2_out, and_4_out, and_3_out);
  xor xor_3 (xor_3_out, and_5_out, and_6_out);
  xor xor_4 (xor_4_out, and_4_out, and_3_out);
  xor xor_5 (xor_5_out, and_7_out, and_8_out);
  xor xor_6 (xor_6_out, and_4_out, and_3_out);
  xor xor_7 (xor_7_out, and_9_out, and_10_out);
  xor xor_8 (xor_8_out, and_4_out, and_3_out);
  D_Flip_Flop d_ff_1 (.D(xor_1_out), .clk(xor_2_out), .Q(O0), .reset(MReset));  // open: Qn, preset
  LED led_1 (.in(O0));
  D_Flip_Flop d_ff_2 (.D(xor_3_out), .clk(xor_4_out), .Q(O1), .reset(MReset));  // open: Qn, preset
  D_Flip_Flop d_ff_3 (.D(xor_5_out), .clk(xor_6_out), .Q(O2), .reset(MReset));  // open: Qn, preset
  D_Flip_Flop d_ff_4 (.D(xor_7_out), .clk(xor_8_out), .Q(O3), .reset(MReset));  // open: Qn, preset
  D_Flip_Flop d_ff_5 (.D(O0), .clk(xor_2_out), .Q(P0), .reset(MReset));  // open: Qn, preset
  D_Flip_Flop d_ff_6 (.D(O1), .clk(xor_4_out), .Q(P1), .reset(MReset));  // open: Qn, preset
  LED led_2 (.in(O1));
  D_Flip_Flop d_ff_7 (.D(O2), .clk(xor_6_out), .Q(P2), .reset(MReset));  // open: Qn, preset
  LED led_3 (.in(O2));
  D_Flip_Flop d_ff_8 (.D(O3), .clk(xor_8_out), .Q(P3), .reset(MReset));  // open: Qn, preset
  LED led_4 (.in(O3));
  D_Flip_Flop d_ff_9 (.D(P0), .clk(xor_2_out), .Q(Q0), .reset(MReset));  // open: Qn, preset
  LED led_5 (.in(P0));
  LED led_6 (.in(P1));
  LED led_7 (.in(P2));
  LED led_8 (.in(P3));
  LED led_9 (.in(Q0));
  D_Flip_Flop d_ff_10 (.D(P1), .clk(xor_4_out), .Q(Q1), .reset(MReset));  // open: Qn, preset
  LED led_10 (.in(Q1));
  D_Flip_Flop d_ff_11 (.D(P2), .clk(xor_6_out), .Q(Q2), .reset(MReset));  // open: Qn, preset
  LED led_11 (.in(Q2));
  D_Flip_Flop d_ff_12 (.D(P3), .clk(xor_8_out), .Q(Q3), .reset(MReset));  // open: Qn, preset
  LED led_12 (.in(Q3));
  D_Flip_Flop d_ff_13 (.D(Q0), .clk(xor_2_out), .Q(R0), .reset(MReset));  // open: Qn, preset
  D_Flip_Flop d_ff_14 (.D(Q1), .clk(xor_4_out), .Q(R1), .reset(MReset));  // open: Qn, preset
  D_Flip_Flop d_ff_15 (.D(Q2), .clk(xor_6_out), .Q(R2), .reset(MReset));  // open: Qn, preset
  D_Flip_Flop d_ff_16 (.D(Q3), .clk(xor_8_out), .Q(R3), .reset(MReset));  // open: Qn, preset
  D_Flip_Flop d_ff_17 (.D(R0), .clk(xor_2_out), .Q(S0), .reset(MReset));  // open: Qn, preset
  LED led_13 (.in(R0));
  D_Flip_Flop d_ff_18 (.D(R1), .clk(xor_4_out), .Q(S1), .reset(MReset));  // open: Qn, preset
  LED led_14 (.in(R1));
  D_Flip_Flop d_ff_19 (.D(R2), .clk(xor_6_out), .Q(S2), .reset(MReset));  // open: Qn, preset
  LED led_15 (.in(R2));
  D_Flip_Flop d_ff_20 (.D(R3), .clk(xor_8_out), .Q(S3), .reset(MReset));  // open: Qn, preset
  LED led_16 (.in(R3));
  LED led_17 (.in(S0));
  LED led_18 (.in(S1));
  LED led_19 (.in(S2));
  LED led_20 (.in(S3));

  // Notes on the sheet:
  //   0
  //   1
  //   2
  //   3
  //   0
  //   1
  //   2
  //   3
  //   0
  //   1
  //   2
  //   3
  //   0
  //   1
  //   2
  //   3
  //   0
  //   1
  //   2
  //   3
endmodule
